# Fritzing sketch ControlCircuitBoard (saved by Fritzing 1.0.3b)
circuit board: 12.4694cm x 9.91718cm

parts:
  Amperemeter2 = INA219 High Side DC Current Sensor Breakout [part_number=904]
  Amperemeter1 = INA219 High Side DC Current Sensor Breakout [part_number=904]
  Sensors = female pin header, 4 pins [form="♀ (female)"]
  Track = female pin header, 4 pins [form="♀ (female)"]
  Power = female pin header, 2 pins [form="♀ (female)"]
  Motorshield = Adafruit DC+Stepper FeatherWing [part_number="Adafruit #2927"]

nets:
  VCC: Amperemeter2.VCC, Amperemeter1.VCC, Sensors.pin1, Motorshield.+3.3V
  GND: Amperemeter2.GND, Amperemeter1.GND, Sensors.pin2, Power.pin1, Motorshield.GND
  N1: Amperemeter2.SCL, Amperemeter1.SCL, Motorshield.SCL
  N2: Amperemeter2.SDA, Amperemeter1.SDA, Motorshield.SDA
  N3: Amperemeter2.VIN-, Motorshield.M1B
  N4: Amperemeter2.VIN+, Track.pin1
  N5: Amperemeter1.VIN-, Motorshield.M2B
  N6: Amperemeter1.VIN+, Track.pin3
  N7: Sensors.pin3, Motorshield.B
  N8: Sensors.pin4, Motorshield.C
  N9: Track.pin2, Motorshield.M1A
  N10: Track.pin4, Motorshield.M2A
  N11: Power.pin2, Motorshield.VMOTOR

notes:
  Power
  Sensors
  Racetrack
  Car is on Track Detection
  Adafruit x Motorshield
  Revision 1893

custom parts:
  INA219 High Side DC Current Sensor Breakout: This breakout board will solve all your power-monitoring problems. Instead of struggling with two multimeters, you can just use the handy INA219B chip on this breakout to both measure both the high side voltage and DC current draw over I2C with 1% precision. Most current-measuring devices such as our current panel meter are only good for low side measuring. That means that unless you want to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
  Adafruit DC+Stepper FeatherWing: This is the DC Motor + Stepper FeatherWing which will let you use 2 x bi-polar stepper motors or 4 x brushed DC motorx (or 1 stepper and 2 DC motors). Using our Feather Stacking Headers or Feather Female Headers you can connect a FeatherWing on top or bottom of your Feather board and let the board take flight! The original Adafruit Motorshield Kit is one of our most beloved kits, which is why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
